// Logisim project Adder.circ as structural Verilog: 1 circuit, main circuit main
module main (
  input  A,
  input  B,
  input  Cin,
  output SumAB,
  output Sum,
  output CAB,
  output Cout,
  output Ctmp
);

  xor xor_1 (SumAB, A, B);
  and and_1 (CAB, A, B);
  and and_2 (Ctmp, SumAB, Cin);
  or or_1 (Cout, CAB, Ctmp);
  xor xor_2 (Sum, SumAB, Cin);

  // Notes on the sheet:
  //   全加器
endmodule
